# Fritzing sketch PwmLed (saved by Fritzing 0.9.2b)
circuit board: 8.46667cm x 5.64444cm
breadboards: 1

parts:
  Εξάρτημα1 = Arduino Uno (Rev3)
  LED1 = LED - 5mm [color="Red (633nm)" package="5 mm [THT]"]
  R1 = Resistor [tolerance=±1% resistance=220 package=THT]

nets:
  N1: Εξάρτημα1.D13/SCK, R1.Pin_1
  N2: Εξάρτημα1.GND, LED1.cathode
  N3: LED1.anode, R1.Pin_0

// code stored in the sketch: SimpleLed.ino
int led=13;
void setup() {
  pinMode(led,OUTPUT);
}

void loop() {
    digitalWrite(led,HIGH);
    delay(1200);
    digitalWrite(led,LOW);
    delay(100);
}
