# Fritzing sketch piranha_led (saved by Fritzing 0.9.2b)
breadboards: 1

parts:
  Part1 = Arduino Uno (Rev3)
  R1 = Resistor [tolerance=±1% resistance=220 package=THT]
  R3 = Resistor [tolerance=±1% resistance=220 package=THT]
  R2 = Resistor [tolerance=±1% resistance=220 package=THT]
  LED1 = RGB LED (com. cathode, rgb) [package="5 mm [THT]"]

nets:
  N1: Part1.D9_PWM, R2.Pin_0
  N2: Part1.D10_PWM/SS, R3.Pin_0
  N3: Part1.D11_PWM/MOSI, R1.Pin_0
  N4: Part1.5V, LED1.common_cathode
  N5: R1.Pin_1, LED1.green_anode
  N6: R3.Pin_1, LED1.blue_anode
  N7: R2.Pin_1, LED1.red_anode
